# Fritzing sketch luminaria (saved by Fritzing 0.8.3b)
circuit board: 5.74cm x 4.9cm
breadboards: 1

parts:
  U1 = ATTINY45 [package=dip]
  LED1 = LED - 5mm [color="Yellow (585nm)" package="5 mm [THT]"]
  BATT1 = 3xAAA Switchable Battery Pack w/Bare Wire
  R1 = Resistor [tolerance=±5% resistance=10k power=125mW package=THT]
  R2 = Resistor [tolerance=±5% resistance=150 power=250mW package=THT]
  C2 = Electrolytic Capacitor [capacitance=10µF voltage=35V package="100 mil [THT, electrolytic]"]
  S1 = Toggle Switch [package=THT]
  C1 = Ceramic Capacitor [capacitance=100nF package="200 mil [THT, multilayer]"]

nets:
  N1: U1.PB5(NRES), R1.Pin_0
  N2: U1.GND, LED1.cathode, BATT1.NEG, C2.-, C1.1
  N3: U1.PB0(MOSI), R2.Pin_1
  N4: U1.VCC, R1.Pin_1, C2.+, S1.L2, C1.0
  N5: LED1.anode, R2.Pin_0
  N6: BATT1.POS, S1.L1, S1.COM

notes:
  luminaria
  by peter (2013)
  <on/off>
  sites.google.com/site/creationsbypeter
  R
  B
  +
  -

custom parts:
  3xAAA Switchable Battery Pack w/Bare Wire: 3xAAA Switchable Battery Pack w/Bare Wire Connectors
